// Logisim project Assignment1.circ as structural Verilog: 11 circuits, main circuit Not
module Not (
  input  in_1,
  output out_2
);

  nand nand_1 (out_2, in_1, in_1);

  // Notes on the sheet:
  //   Use only a built-in Nand gate for this (found in Gates>NAND).
  //   Once you are done go to Simulate>Test Vector.
  //   Select the Not.txt file, and run it to try the test cases
  //   Not Gate
endmodule

module And (
  input  in_1,
  input  in_2,
  output out_3
);

  wire nand_1_out;

  nand nand_1 (nand_1_out, in_1, in_2);
  not nand_2 (out_3, nand_1_out);  // NAND_Gate

  // Notes on the sheet:
  //   Simple Gate Implementation using Nand and Not
  //   For all gates in this assignment (except Nand),you are required to use
  //   the custom subcircuits you build, rather than the built-in gates.
  //   And Gate
endmodule

module Or (
  input  in_1,
  input  in_2,
  output out
);

  wire nand_1_out, nand_2_out;

  nand nand_1 (nand_1_out, in_1, in_1);
  nand nand_2 (nand_2_out, in_2, in_2);
  nand nand_3 (out, nand_1_out, nand_2_out);

  // Notes on the sheet:
  //   This function can be defined in terms of boolean expressions previously implemented
  //   It helps to start by looking at the expression as Not(Not(A Or B)) and using boolean
  //   algebra to transform this into something we can implement
  //   Or Gate
endmodule

module Xor (
  input  in_1,
  input  in_2,
  output out
);

  wire nand_1_out, nand_2_out, nand_3_out;

  nand nand_1 (nand_1_out, in_1, in_2);
  nand nand_2 (nand_2_out, in_1, nand_1_out);
  nand nand_3 (nand_3_out, nand_1_out, in_2);
  nand nand_4 (out, nand_2_out, nand_3_out);

  // Notes on the sheet:
  //   This function can also be defined in terms of boolean expressions already created. 
  //   Try to express what the Xor gate does in english, then translate that to a boolean
  //   expression that you can implement!
  //   Xor Gate
endmodule

module Mux (
  input  a,
  input  sel,
  input  b,
  output out
);

  wire and_1_out_3, and_2_out_3, not_1_out_2;

  Not not_1 (.in_1(sel), .out_2(not_1_out_2));
  And and_1 (.in_1(sel), .in_2(b), .out_3(and_1_out_3));
  And and_2 (.in_1(a), .in_2(not_1_out_2), .out_3(and_2_out_3));
  Or or_1 (.in_1(and_2_out_3), .in_2(and_1_out_3), .out(out));

  // Notes on the sheet:
  //   Function:
  //   If sel == 0, out = a;
  //   	else out = b;
  //   Can be implemented with And, or and Not. Try a truth table!
endmodule

module DMux (
  input  sel,
  input  in,
  output a,
  output b
);

  wire not_1_out_2;

  Not not_1 (.in_1(sel), .out_2(not_1_out_2));
  And and_1 (.in_1(in), .in_2(sel), .out_3(b));
  And and_2 (.in_1(not_1_out_2), .in_2(in), .out_3(a));

  // Notes on the sheet:
  //   Function:
  //   If sel == 0, [a, b] = [in, 0]
  //   	else, [a, b] = [0, in]
  //   Same as before, use a truth table and basic logic gates.
endmodule

module Not16 (
  input  [15:0] in,
  output [15:0] out
);

  Not not_1 (.in_1(in[0]), .out_2(out[0]));
  Not not_2 (.in_1(in[1]), .out_2(out[1]));
  Not not_3 (.in_1(in[2]), .out_2(out[2]));
  Not not_4 (.in_1(in[3]), .out_2(out[3]));
  Not not_5 (.in_1(in[4]), .out_2(out[4]));
  Not not_6 (.in_1(in[5]), .out_2(out[5]));
  Not not_7 (.in_1(in[6]), .out_2(out[6]));
  Not not_8 (.in_1(in[7]), .out_2(out[7]));
  Not not_9 (.in_1(in[8]), .out_2(out[8]));
  Not not_10 (.in_1(in[9]), .out_2(out[9]));
  Not not_11 (.in_1(in[10]), .out_2(out[10]));
  Not not_12 (.in_1(in[11]), .out_2(out[11]));
  Not not_13 (.in_1(in[12]), .out_2(out[12]));
  Not not_14 (.in_1(in[13]), .out_2(out[13]));
  Not not_15 (.in_1(in[14]), .out_2(out[14]));
  Not not_16 (.in_1(in[15]), .out_2(out[15]));

  // Notes on the sheet:
  //   Function:
  //   For all i from 0 .. 15, out[i] = Not(in[i])
  //   These are rather repetitive, you will use the splitter element (shown below)
  //   a lot. You already have an elementary version of each of these gates, the implementation
  //   of a 16-bit gate is just a matter of constructing an array of n elementary gates, where
  //   each gate operates separately on each bit.
  //   Changing the spacing attribute on the splitter can help a lot for these
endmodule

module And16 (
  input  [15:0] a,
  input  [15:0] b,
  output [15:0] out
);

  And and_1 (.in_1(a[0]), .in_2(b[0]), .out_3(out[0]));
  And and_2 (.in_1(a[1]), .in_2(b[1]), .out_3(out[1]));
  And and_3 (.in_1(a[2]), .in_2(b[2]), .out_3(out[2]));
  And and_4 (.in_1(a[3]), .in_2(b[3]), .out_3(out[3]));
  And and_5 (.in_1(a[4]), .in_2(b[4]), .out_3(out[4]));
  And and_6 (.in_1(a[5]), .in_2(b[5]), .out_3(out[5]));
  And and_7 (.in_1(a[6]), .in_2(b[6]), .out_3(out[6]));
  And and_8 (.in_1(a[7]), .in_2(b[7]), .out_3(out[7]));
  And and_9 (.in_1(a[8]), .in_2(b[8]), .out_3(out[8]));
  And and_10 (.in_1(a[9]), .in_2(b[9]), .out_3(out[9]));
  And and_11 (.in_1(a[10]), .in_2(b[10]), .out_3(out[10]));
  And and_12 (.in_1(a[11]), .in_2(b[11]), .out_3(out[11]));
  And and_13 (.in_1(a[12]), .in_2(b[12]), .out_3(out[12]));
  And and_14 (.in_1(a[13]), .in_2(b[13]), .out_3(out[13]));
  And and_15 (.in_1(a[14]), .in_2(b[14]), .out_3(out[14]));
  And and_16 (.in_1(a[15]), .in_2(b[15]), .out_3(out[15]));

  // Notes on the sheet:
  //   Function:
  //   For all i from 0 .. 15, out[i] = And(in[i])
endmodule

module Or16 (
  input  [15:0] a,
  input  [15:0] b,
  output [15:0] out
);

  Or or_1 (.in_1(a[0]), .in_2(b[0]), .out(out[0]));
  Or or_2 (.in_1(a[1]), .in_2(b[1]), .out(out[1]));
  Or or_3 (.in_1(a[2]), .in_2(b[2]), .out(out[2]));
  Or or_4 (.in_1(a[3]), .in_2(b[3]), .out(out[3]));
  Or or_5 (.in_1(a[4]), .in_2(b[4]), .out(out[4]));
  Or or_6 (.in_1(a[5]), .in_2(b[5]), .out(out[5]));
  Or or_7 (.in_1(a[6]), .in_2(b[6]), .out(out[6]));
  Or or_8 (.in_1(a[7]), .in_2(b[7]), .out(out[7]));
  Or or_9 (.in_1(a[8]), .in_2(b[8]), .out(out[8]));
  Or or_10 (.in_1(a[9]), .in_2(b[9]), .out(out[9]));
  Or or_11 (.in_1(a[10]), .in_2(b[10]), .out(out[10]));
  Or or_12 (.in_1(a[11]), .in_2(b[11]), .out(out[11]));
  Or or_13 (.in_1(a[12]), .in_2(b[12]), .out(out[12]));
  Or or_14 (.in_1(a[13]), .in_2(b[13]), .out(out[13]));
  Or or_15 (.in_1(a[14]), .in_2(b[14]), .out(out[14]));
  Or or_16 (.in_1(a[15]), .in_2(b[15]), .out(out[15]));

  // Notes on the sheet:
  //   Function:
  //   For all i from 0 .. 15, out[i] = Or(in[i])
endmodule

module Mux16 (
  input  [15:0] a,
  input  sel,
  input  [15:0] b,
  output [15:0] out
);

  Mux mux_1 (.a(a[0]), .sel(sel), .b(b[0]), .out(out[0]));
  Mux mux_2 (.a(a[1]), .sel(sel), .b(b[1]), .out(out[1]));
  Mux mux_3 (.a(a[2]), .sel(sel), .b(b[2]), .out(out[2]));
  Mux mux_4 (.a(a[3]), .sel(sel), .b(b[3]), .out(out[3]));
  Mux mux_5 (.a(a[4]), .sel(sel), .b(b[4]), .out(out[4]));
  Mux mux_6 (.a(a[5]), .sel(sel), .b(b[5]), .out(out[5]));
  Mux mux_7 (.a(a[6]), .sel(sel), .b(b[6]), .out(out[6]));
  Mux mux_8 (.a(a[7]), .sel(sel), .b(b[7]), .out(out[7]));
  Mux mux_9 (.a(a[8]), .sel(sel), .b(b[8]), .out(out[8]));
  Mux mux_10 (.a(a[9]), .sel(sel), .b(b[9]), .out(out[9]));
  Mux mux_11 (.a(a[10]), .sel(sel), .b(b[10]), .out(out[10]));
  Mux mux_12 (.a(a[11]), .sel(sel), .b(b[11]), .out(out[11]));
  Mux mux_13 (.a(a[12]), .sel(sel), .b(b[12]), .out(out[12]));
  Mux mux_14 (.a(a[13]), .sel(sel), .b(b[13]), .out(out[13]));
  Mux mux_15 (.a(a[14]), .sel(sel), .b(b[14]), .out(out[14]));
  Mux mux_16 (.a(a[15]), .sel(sel), .b(b[15]), .out(out[15]));

  // Notes on the sheet:
  //   Function:
  //   If sel == 0, out = a
  //   	else, out = b
  //   An n-bit multiplexer is just the result of feeding the same selection bit
  //   into n 1-bit multiplexers. Again, splitters and lots of the elementary version
  //   of the gate.
endmodule

module Or8Way (
  input  [7:0] in,
  output out
);

  wire or_1_out, or_2_out, or_3_out, or_4_out, or_5_out, or_6_out;

  Or or_1 (.in_1(in[0]), .in_2(in[1]), .out(or_1_out));
  Or or_2 (.in_1(in[2]), .in_2(in[3]), .out(or_2_out));
  Or or_3 (.in_1(in[4]), .in_2(in[5]), .out(or_3_out));
  Or or_4 (.in_1(in[6]), .in_2(in[7]), .out(or_4_out));
  Or or_5 (.in_1(or_1_out), .in_2(or_2_out), .out(or_5_out));
  Or or_6 (.in_1(or_3_out), .in_2(or_4_out), .out(or_6_out));
  Or or_7 (.in_1(or_5_out), .in_2(or_6_out), .out(out));

  // Notes on the sheet:
  //   Function:
  //   Out = in[0] Or in[1] Or ... Or in[7]
  //   Think forks for this one
  //   Try to get a 3-way Or gate first, then use the same process for the 8-way
  //   or gate. 
endmodule
