// Logisim project Assignment4_b.circ as structural Verilog: 4 circuits, main circuit RAM512
module RAM64 (
  input  [5:0] address,
  input  load,
  input  [15:0] in,
  output [15:0] out
);

  wire clock_1_out;

  RAM #(.addrWidth(6), .dataWidth(16)) ram_1 (
    .addr(address), .we(load), .clk(clock_1_out), .din(in), .dout(out));  // open: oe
  Clock clock_1 (.out(clock_1_out));

  // Notes on the sheet:
  //   With the recursive approach for building RAM, there are too many gates for the simulator, and this leads to performance
  //   issues. For this reason, we have separated the assignment into two halves. This subcircuit is already completed and uses
  //   the built-in RAM module.
  //   RAM64 x 64 means that the address space has 64 registers, each containing 16 bits. Write-Enable is the same
  //   as the Load Input. C3 is for a clock input (you will need to connect a clock). The rightmost port is the output
  //   data, the upper left port is the address and the bottom left port is the incoming data.
  //   You will use the built-in RAM for a future assignment. I recommend playing around with it!
endmodule

module RAM512 (
  input  load,
  input  [8:0] address,
  input  [15:0] in,
  output [15:0] out
);


  // Notes on the sheet:
  //   RAM512 can be built out of multiple RAM64 chips in a similar fashion to how
  //   RAM64 was constructed.
endmodule

module RAM4K (
  input  load,
  input  [11:0] address,
  input  [15:0] in,
  output [15:0] out
);


  // Notes on the sheet:
  //   Use the previously implemented RAM512 chip for this chip
endmodule

module RAM16K (
  input  load,
  input  [13:0] address,
  input  [15:0] in,
  output [15:0] out
);


  // Notes on the sheet:
  //   Use the previously implemented RAM4K for this chip.
endmodule
